# Fritzing sketch Untitled Sketch 2 (saved by Fritzing 0.9.3b)

parts:
  Part1 = Arduino Mega 2560 (Rev3)
  S1 = H-Bridge with L298N
  M1 = DC Motor
  M2 = DC Motor
  M3 = DC Motor
  M4 = DC Motor
  U1 = BATTERY-2 [package=battery-aa]
  U2 = BATTERY-2 [package=battery-aa]
  U3 = BATTERY-2 [package=battery-aa]
  Gizwits_WiFi_Witty_ESP-12F1 = Gizwits WiFi Witty ESP-12F

nets:
  N1: Part1.D15/RX3, Gizwits_WiFi_Witty_ESP-12F1.TXD
  N2: Part1.D14/TX3, Gizwits_WiFi_Witty_ESP-12F1.RXD
  3V3: Part1.3V3, Gizwits_WiFi_Witty_ESP-12F1.VCC
  GND: Part1.GND, S1.GND, U1.-1, Gizwits_WiFi_Witty_ESP-12F1.GND
  VIN: Part1.VIN, S1.12V, U2.+1
  N3: Part1.D2_PWM, S1.ENA
  N4: Part1.D3_PWM, S1.IN1
  N5: Part1.D4_PWM, S1.IN2
  N6: Part1.D5_PWM, S1.ENB
  N7: Part1.D6_PWM, S1.IN3
  N8: Part1.D7_PWM, S1.IN4
  N9: S1.M1-01, M1.pin_2, M2.pin_2
  N10: S1.M1-02, M1.pin_1, M2.pin_1
  N11: S1.M2-01, M3.pin_2, M4.pin_2
  N12: S1.M2-02, M3.pin_1, M4.pin_1
  N13: U1.+1, U3.-1
  N14: U2.-1, U3.+1

custom parts:
  H-Bridge with L298N: h-bridge
